// Logisim project cpu.circ as structural Verilog: 2 circuits, main circuit main
module main (
);

  wire add, and_2_out, and_3_out, and_4_out, and_5_out, and_6_out, and_7_out, and_8_out, and_9_out, and_alu,
       clk, clock_1_out, Execute, Fetch, hlt, IsALU, jc, jmp, lda, ldb, not_1_out, not_2_out, not_3_out,
       not_4_out, not_alu, or_1_out, or_2_out, or_3_out, or_alu, prt, shl, shr, sta, stb, sub, t_ff_1_q,
       xor_alu;
  wire [2:0] alu_1_negative, flags, OpALU;
  wire [3:0] addr, IR_q, PC_q;
  wire [7:0] A_q, alu_1_result, B_q, dbus, multiplexer_1_out, STDOUT_q;

  Clock clock_1 (.out(clock_1_out));
  and and_1 (clk, clock_1_out, not_1_out);
  not not_1 (not_1_out, hlt);
  T_Flip_Flop t_ff_1 (.T(1'b1), .clk(not_2_out), .Q(t_ff_1_q));  // open: Qn, reset, preset
  not not_2 (not_2_out, clk);
  Register IR (.D(dbus), .en(Fetch), .clk(clk), .Q({IsALU, OpALU, IR_q}));  // open: clr
  Decoder decoder_1 (.out0(Fetch), .out1(Execute), .sel(t_ff_1_q));  // open: en
  Decoder #(.select(4)) decoder_2 (
    .out0(lda), .out1(sta), .out2(ldb), .out3(stb), .out4(jmp), .out5(jc), .out6(prt), .out7(hlt),
    .out8(and_alu), .out9(or_alu), .out10(xor_alu), .out11(not_alu), .out12(shl), .out13(shr), .out14(add),
    .out15(sub), .sel({IsALU, OpALU}));  // open: en
  assign addr = Execute ? IR_q : 4'bz;  // Controlled_Buffer controlled_buffer_1
  and and_2 (and_2_out, ldb, Execute);
  and and_3 (and_3_out, jc, flags[2]);
  or or_1 (or_1_out, lda, IsALU);
  and and_4 (and_4_out, or_1_out, Execute);
  Register B (.D(dbus), .en(and_2_out), .clk(clk), .Q(B_q));  // open: clr
  or or_2 (or_2_out, jmp, and_3_out);
  Multiplexer #(.width(8)) multiplexer_1 (.in0(alu_1_result), .in1(dbus), .out(multiplexer_1_out), .sel(not_3_out));
  not not_3 (not_3_out, IsALU);
  assign dbus = and_5_out ? B_q : 8'bz;  // Controlled_Buffer controlled_buffer_2
  and and_5 (and_5_out, stb, Execute);
  Counter #(.max('hf), .width(4)) PC (
    .load(or_2_out), .D(addr), .count(Fetch), .Q(PC_q), .up(1'b1), .clk(clk));  // open: carry, clr
  and and_6 (and_6_out, sta, Execute);
  Register A (.D(multiplexer_1_out), .en(and_4_out), .clk(clk), .Q(A_q));  // open: clr
  assign addr = Fetch ? PC_q : 4'bz;  // Controlled_Buffer controlled_buffer_3
  assign dbus = and_6_out ? A_q : 8'bz;  // Controlled_Buffer controlled_buffer_4
  ALU alu_1 (
    .Result(alu_1_result), .Zero(alu_1_negative[1]), .Negative(alu_1_negative[0]),
    .CarryOut(alu_1_negative[2]), .A(A_q), .B(dbus), .Opcode(OpALU));
  and and_7 (and_7_out, Execute, IsALU);
  Register #(.width(3)) u_FLAGS (.D(alu_1_negative), .en(and_7_out), .clk(clk), .Q(flags));  // open: clr
  or or_3 (or_3_out, sta, stb);
  and and_8 (and_8_out, prt, Execute);
  RAM #(.addrWidth(4), .asyncread("true"), .databus("bidir")) ram_1 (
    .addr(addr), .we(and_9_out), .oe(not_4_out), .clk(clk), .data(dbus));
  and and_9 (and_9_out, or_3_out, Execute);
  not not_4 (not_4_out, and_9_out);
  Register STDOUT (.D(dbus), .en(and_8_out), .clk(clk), .Q(STDOUT_q));  // open: clr
  _7_Segment_Display u_7_segment_display_1 ();  // open: g, f, a, b, e, d, c, dp
  // BCD_to_7_Segment_decoder bcd_to_7_segment_decoder_1: pin names not known
  // Binary_to_BCD_converter #(.binvalue(8)) binary_to_bcd_converter_1: pin names not known; wires that end beside it: STDOUT_q
  _7_Segment_Display u_7_segment_display_2 ();  // open: g, f, a, b, e, d, c, dp
  // BCD_to_7_Segment_decoder bcd_to_7_segment_decoder_2: pin names not known
  _7_Segment_Display u_7_segment_display_3 ();  // open: g, f, a, b, e, d, c, dp
  // BCD_to_7_Segment_decoder bcd_to_7_segment_decoder_3: pin names not known
endmodule

module ALU (
  input  [7:0] A,
  input  [7:0] B,
  input  [2:0] Opcode,
  output [7:0] Result,
  output Zero,
  output Negative,
  output CarryOut
);

  wire adder_1_cout, and_2_out, and_3_out, decoder_1_out6, decoder_1_out7, subtractor_1_bout;
  wire [7:0] adder_1_out, and_1_out, not_1_out, or_1_out, shifter_1_out, shifter_2_out, subtractor_1_out,
       xor_1_out;

  assign and_1_out = A & B;  // AND_Gate and_1, 8 bits wide
  assign or_1_out = A | B;  // OR_Gate or_1, 8 bits wide
  assign xor_1_out = A ^ B;  // XOR_Gate xor_1, 8 bits wide
  assign not_1_out = ~A;  // NOT_Gate not_1, 8 bits wide
  Shifter shifter_1 (.in(A), .\dist (B[2:0]), .out(shifter_1_out));
  Shifter #(.shift("lr")) shifter_2 (.in(A), .\dist (B[2:0]), .out(shifter_2_out));
  Adder adder_1 (.a(A), .b(B), .out(adder_1_out), .cout(adder_1_cout));  // open: cin
  Subtractor subtractor_1 (.a(A), .b(B), .out(subtractor_1_out), .bout(subtractor_1_bout));  // open: bin
  Multiplexer #(.select(3), .width(8)) multiplexer_1 (
    .in0(and_1_out), .in1(or_1_out), .in2(xor_1_out), .in3(not_1_out), .in4(shifter_1_out),
    .in5(shifter_2_out), .in6(adder_1_out), .in7(subtractor_1_out), .out({Negative, Result[6:0]}),
    .sel(Opcode));
  Decoder #(.select(3)) decoder_1 (
    .out6(decoder_1_out6), .out7(decoder_1_out7), .sel(Opcode));  // open: out0, out1, out2, out3, out4, out5, en
  nor nor_1 (Zero, Result[0], Result[1], Result[2], Result[3], Result[4], Result[5], Result[6], Negative);
  and and_2 (and_2_out, adder_1_cout, decoder_1_out6);
  and and_3 (and_3_out, subtractor_1_bout, decoder_1_out7);
  or or_2 (CarryOut, and_2_out, and_3_out);

  assign Result[7] = Negative;
endmodule
